// Logisim project RV32I_base.circ as structural Verilog: 8 circuits, main circuit RegisterFile
module main (
  input  [31:0] INST,
  output out_2,
  output [3:0] out_3,
  output [4:0] out_4,
  output out_5,
  output out_6,
  output [1:0] out_7,
  output [3:0] out_8,
  output out_9,
  output out_10,
  output out_11,
  output out_12,
  output [31:0] out_13
);

  wire clk;
  wire [31:0] adder_1_out, alu_1_out_4, d_mem_1_out_5, immgen_1_out_3, multiplexer_1_out, multiplexer_2_out,
       multiplexer_3_out, register_1_q, registerfile_1_data_a, registerfile_1_data_b;

  Clock clock_1 (.out(clk));
  Multiplexer #(.width(32), .enable("false")) multiplexer_1 (
    .in0(adder_1_out), .in1(alu_1_out_4), .out(multiplexer_1_out), .sel(out_9));
  Register #(.width(32)) register_1 (.D(multiplexer_1_out), .en(1'b1), .clk(clk), .Q(register_1_q), .clr(1'b0));
  I_MEM i_mem_1 (.in_1(register_1_q));  // open: out_2
  Adder #(.width(32)) adder_1 (.a(register_1_q), .b(32'h4), .out(adder_1_out), .cin(1'b0));  // open: cout
  ControlUnit controlunit_1 (
    .in_1(INST), .RegWrite(out_2), .ALUSrcA(out_6), .ALUSrcB(out_5), .WBSel(out_7), .PCSel(out_9),
    .MemRW(out_8), .BrEq(out_11), .BrLT(out_12), .BrUn(out_10), .ALUOp(out_3), .ImmSrc(out_4));
  RegisterFile registerfile_1 (
    .DATA_A(registerfile_1_data_a), .DATA_B(registerfile_1_data_b), .ADDR_IN(INST[11:7]), .DATA_IN(out_13),
    .LOAD(out_2), .ADDR_A(INST[19:15]), .ADDR_B(INST[24:20]), .CLK(clk));
  ImmGen immgen_1 (.in_1(out_4), .in_2(INST[31:7]), .out_3(immgen_1_out_3));
  BranchCom branchcom_1 (
    .in_1(registerfile_1_data_a), .in_2(registerfile_1_data_b), .BrEq(out_11), .BrLT(out_12), .BrUn(out_10));
  ALU alu_1 (.ALUSrcA(multiplexer_2_out), .in_3(multiplexer_3_out), .in_1(out_3), .out_4(alu_1_out_4));
  Multiplexer #(.width(32), .enable("false")) multiplexer_2 (
    .in0(registerfile_1_data_a), .in1(register_1_q), .out(multiplexer_2_out), .sel(out_6));
  Multiplexer #(.width(32), .enable("false")) multiplexer_3 (
    .in0(registerfile_1_data_b), .in1(immgen_1_out_3), .out(multiplexer_3_out), .sel(out_5));
  D_MEM d_mem_1 (.in_3(clk), .in_4(registerfile_1_data_b), .out_5(d_mem_1_out_5), .in_2(alu_1_out_4), .in_1(out_8));
  Multiplexer #(.select(2), .width(32), .enable("false")) multiplexer_4 (
    .in0(alu_1_out_4), .in1(d_mem_1_out_5), .in2(adder_1_out), .out(out_13), .sel(out_7));  // open: in3

  // Other names for the same wires on the sheet: ALUOp[3:0] = out_3; ALUSrcA = out_6; ALUSrcB = out_5; BrEq = out_11;
  //   BrLT = out_12; BrUn = out_10; ImmSrc[4:0] = out_4; MemRW[3:0] = out_8; PCSel = out_9; RegWrite = out_2;
  //   WBSel[1:0] = out_7

  // Notes on the sheet:
  //   RISC-V Single Cycle Datapath
endmodule

module ControlUnit (
  input  [31:0] in_1,
  input  BrEq,
  input  BrLT,
  output [3:0] MemRW,
  output [3:0] ALUOp,
  output BrUn,
  output RegWrite,
  output ALUSrcA,
  output ALUSrcB,
  output [1:0] WBSel,
  output [4:0] ImmSrc,
  output PCSel
);

  wire and_1_out, and_2_out, and_3_out, and_4_out, and_9_out, and_12_out, and_13_out, and_14_out, and_17_out,
       and_18_out, and_19_out, and_20_out, and_21_out, bitselector_1_out, not_1_out, not_2_out, not_3_out,
       not_4_out, not_5_out, not_6_out, not_7_out, not_8_out, not_9_out, not_10_out, not_11_out, not_12_out,
       not_13_out, not_15_out, not_16_out, not_17_out, or_1_out, or_5_out, or_7_out;
  wire [3:0] multiplexer_1_out, multiplexer_2_out;

  not not_1 (not_1_out, in_1[6]);
  not not_2 (not_2_out, in_1[3]);
  not not_3 (not_3_out, in_1[2]);
  not not_4 (not_4_out, in_1[6]);
  not not_5 (not_5_out, in_1[5]);
  not not_6 (not_6_out, in_1[3]);
  not not_7 (not_7_out, in_1[2]);
  and and_1 (and_1_out, in_1[14], ~in_1[13], in_1[12]);  // AND_Gate
  and and_2 (and_2_out, ~in_1[14], ~in_1[13], in_1[12]);  // AND_Gate
  not not_8 (not_8_out, in_1[6]);
  not not_9 (not_9_out, in_1[4]);
  not not_10 (not_10_out, in_1[3]);
  not not_11 (not_11_out, in_1[2]);
  not not_12 (not_12_out, in_1[4]);
  not not_13 (not_13_out, in_1[4]);
  // NOT_Gate not_14 has open pins: in=in_1[3], out=open
  not not_15 (not_15_out, in_1[2]);
  not not_16 (not_16_out, in_1[6]);
  not not_17 (not_17_out, in_1[3]);
  and and_3 (and_3_out, not_1_out, in_1[5], in_1[4], not_2_out, not_3_out);
  and and_4 (and_4_out, not_4_out, not_5_out, not_6_out, not_7_out);
  or or_1 (or_1_out, and_1_out, and_2_out);
  and and_5 (ImmSrc[0], not_8_out, in_1[5], not_9_out, not_10_out, not_11_out);
  and and_6 (WBSel[1], in_1[6], in_1[5], not_12_out, in_1[2]);
  and and_7 (ImmSrc[1], in_1[6], in_1[5], not_13_out, not_15_out);
  and and_8 (ImmSrc[2], not_16_out, in_1[4], not_17_out, in_1[2]);
  or or_2 (RegWrite, and_3_out, and_4_out, WBSel[1], ImmSrc[2]);
  and and_9 (and_9_out, in_1[4], and_4_out);
  and and_10 (WBSel[0], and_4_out, ~in_1[4]);  // AND_Gate
  and and_11 (ImmSrc[3], in_1[3], WBSel[1]);
  and and_12 (and_12_out, WBSel[1], ~in_1[3]);  // AND_Gate
  and and_13 (and_13_out, in_1[5], ImmSrc[2]);
  and and_14 (and_14_out, ImmSrc[2], ~in_1[5]);  // AND_Gate
  or or_3 (ALUSrcA, ImmSrc[3], ImmSrc[1], and_14_out);
  or or_4 (ALUSrcB, and_4_out, ImmSrc[0], WBSel[1], ImmSrc[1], ImmSrc[2]);
  Multiplexer #(.width(4), .enable("false")) multiplexer_1 (
    .in0({in_1[30], in_1[14:12]}), .in1({1'b0, in_1[14:12]}), .out(multiplexer_1_out), .sel(ImmSrc[4]));
  and and_15 (ImmSrc[4], and_9_out, or_1_out);
  Multiplexer #(.width(4), .enable("false")) multiplexer_2 (
    .in0(multiplexer_1_out), .in1(4'b1001), .out(multiplexer_2_out), .sel(and_13_out));
  Multiplexer #(.width(4), .enable("false")) multiplexer_3 (
    .in0(multiplexer_2_out), .in1(4'b0000), .out(ALUOp), .sel(or_5_out));
  or or_5 (or_5_out, WBSel[0], ImmSrc[0], WBSel[1], ImmSrc[1], and_14_out);
  and and_16 (BrUn, bitselector_1_out, ImmSrc[1]);
  BitSelector #(.width(3)) bitselector_1 (.in(in_1[14:12]), .out(bitselector_1_out), .sel(2'b01));
  or or_6 (PCSel, and_12_out, ImmSrc[3], and_17_out);
  and and_17 (and_17_out, ImmSrc[1], or_7_out);
  and and_18 (and_18_out, ~in_1[14], ~in_1[12], BrEq);  // AND_Gate
  and and_19 (and_19_out, ~in_1[14], in_1[12], ~BrEq);  // AND_Gate
  or or_7 (or_7_out, and_18_out, and_19_out, and_20_out, and_21_out);
  and and_20 (and_20_out, in_1[14], ~in_1[12], BrLT);  // AND_Gate
  and and_21 (and_21_out, in_1[14], in_1[12], ~BrLT);  // AND_Gate

  assign MemRW = {ImmSrc[0], in_1[14:12]};

  // Notes on the sheet:
  //   ImmSrc: pull=down
  //   WBSel: pull=down
  //   ALUOp: pull=down
  //   MemRW: pull=down
  //   ALUSrcB: pull=down
  //   Instr[31:0]
  //   R_Type
  //   Decode for SRAI,SRLI,SLLI
  //   S_Type (Store)
  //   Jump
  //   B_Type
  //   U_Type
  //   Reg I_Type
  //   Mem I_Type
  //   J_Type
  //   JALR
  //   LUI
  //   AUIPC
  //   r-type
  //   shamt
  //   LUI
  //   add
  //   ImmSrc
  //   000000: I_Type
  //   000001: S_Type
  //   000010: B_Type
  //   000100: U_Type
  //   001000: J_Type
  //   010000: shamt
  //   WBSel
  //   00: ALU
  //   10: PC+4
  //   01: D_MEM
  //   MemRW
  //   0000: Load Byte
  //   0010: Load Word
  //   1000: Store Byte
  //   1010: Store Word
  //   0001: Load Half-word
  //   0100: Load Byte Unsigned
  //   0101: Load: Half-word Unsigned
  //   1001: Store Half-word
endmodule

module RegisterFile (
  input  [31:0] DATA_IN,
  input  CLK,
  input  LOAD,
  input  [4:0] ADDR_IN,
  input  [4:0] ADDR_A,
  input  [4:0] ADDR_B,
  output [31:0] DATA_A,
  output [31:0] DATA_B
);

  wire and_1_out, and_2_out, and_3_out, and_4_out, and_5_out, and_6_out, and_7_out, and_8_out, and_9_out,
       and_10_out, and_11_out, and_12_out, and_13_out, and_14_out, and_15_out, and_16_out, and_17_out,
       and_18_out, and_19_out, and_20_out, and_21_out, and_22_out, and_23_out, and_24_out, and_25_out,
       and_26_out, and_27_out, and_28_out, and_29_out, and_30_out, and_31_out, and_32_out, decoder_1_out0,
       decoder_1_out1, decoder_1_out2, decoder_1_out3, decoder_1_out4, decoder_1_out5, decoder_1_out6,
       decoder_1_out7, decoder_1_out8, decoder_1_out9, decoder_1_out10, decoder_1_out11, decoder_1_out12,
       decoder_1_out13, decoder_1_out14, decoder_1_out15, decoder_1_out16, decoder_1_out17, decoder_1_out18,
       decoder_1_out19, decoder_1_out20, decoder_1_out21, decoder_1_out22, decoder_1_out23, decoder_1_out24,
       decoder_1_out25, decoder_1_out26, decoder_1_out27, decoder_1_out28, decoder_1_out29, decoder_1_out30,
       decoder_1_out31;
  wire [31:0] register_1_q, register_2_q, register_3_q, register_4_q, register_5_q, register_6_q,
       register_7_q, register_8_q, register_9_q, register_10_q, register_11_q, register_12_q, register_13_q,
       register_14_q, register_15_q, register_16_q, register_17_q, register_18_q, register_19_q,
       register_20_q, register_21_q, register_22_q, register_23_q, register_24_q, register_25_q,
       register_26_q, register_27_q, register_28_q, register_29_q, register_30_q, register_31_q,
       register_32_q;

  Decoder #(.select(5), .enable("false")) decoder_1 (
    .out0(decoder_1_out0), .out1(decoder_1_out1), .out2(decoder_1_out2), .out3(decoder_1_out3),
    .out4(decoder_1_out4), .out5(decoder_1_out5), .out6(decoder_1_out6), .out7(decoder_1_out7),
    .out8(decoder_1_out8), .out9(decoder_1_out9), .out10(decoder_1_out10), .out11(decoder_1_out11),
    .out12(decoder_1_out12), .out13(decoder_1_out13), .out14(decoder_1_out14), .out15(decoder_1_out15),
    .out16(decoder_1_out16), .out17(decoder_1_out17), .out18(decoder_1_out18), .out19(decoder_1_out19),
    .out20(decoder_1_out20), .out21(decoder_1_out21), .out22(decoder_1_out22), .out23(decoder_1_out23),
    .out24(decoder_1_out24), .out25(decoder_1_out25), .out26(decoder_1_out26), .out27(decoder_1_out27),
    .out28(decoder_1_out28), .out29(decoder_1_out29), .out30(decoder_1_out30), .out31(decoder_1_out31),
    .sel(ADDR_IN));
  Register #(.width(32)) register_1 (.D({32{1'b0}}), .en(and_1_out), .clk(CLK), .Q(register_1_q), .clr(1'b0));
  and and_1 (and_1_out, LOAD, decoder_1_out0);
  Register #(.width(32)) register_2 (.D(DATA_IN), .en(and_2_out), .clk(CLK), .Q(register_2_q), .clr(1'b0));
  and and_2 (and_2_out, LOAD, decoder_1_out1);
  Register #(.width(32)) register_3 (.D(DATA_IN), .en(and_3_out), .clk(CLK), .Q(register_3_q), .clr(1'b0));
  and and_3 (and_3_out, LOAD, decoder_1_out2);
  Register #(.width(32)) register_4 (.D(DATA_IN), .en(and_4_out), .clk(CLK), .Q(register_4_q), .clr(1'b0));
  and and_4 (and_4_out, LOAD, decoder_1_out3);
  Register #(.width(32)) register_5 (.D(DATA_IN), .en(and_5_out), .clk(CLK), .Q(register_5_q), .clr(1'b0));
  and and_5 (and_5_out, LOAD, decoder_1_out4);
  Register #(.width(32)) register_6 (.D(DATA_IN), .en(and_6_out), .clk(CLK), .Q(register_6_q), .clr(1'b0));
  and and_6 (and_6_out, LOAD, decoder_1_out5);
  Register #(.width(32)) register_7 (.D(DATA_IN), .en(and_7_out), .clk(CLK), .Q(register_7_q), .clr(1'b0));
  and and_7 (and_7_out, LOAD, decoder_1_out6);
  Register #(.width(32)) register_8 (.D(DATA_IN), .en(and_8_out), .clk(CLK), .Q(register_8_q), .clr(1'b0));
  and and_8 (and_8_out, LOAD, decoder_1_out7);
  Register #(.width(32)) register_9 (.D(DATA_IN), .en(and_9_out), .clk(CLK), .Q(register_9_q), .clr(1'b0));
  and and_9 (and_9_out, LOAD, decoder_1_out8);
  Register #(.width(32)) register_10 (.D(DATA_IN), .en(and_10_out), .clk(CLK), .Q(register_10_q), .clr(1'b0));
  and and_10 (and_10_out, LOAD, decoder_1_out9);
  Register #(.width(32)) register_11 (.D(DATA_IN), .en(and_11_out), .clk(CLK), .Q(register_11_q), .clr(1'b0));
  and and_11 (and_11_out, LOAD, decoder_1_out10);
  Register #(.width(32)) register_12 (.D(DATA_IN), .en(and_12_out), .clk(CLK), .Q(register_12_q), .clr(1'b0));
  and and_12 (and_12_out, LOAD, decoder_1_out11);
  Register #(.width(32)) register_13 (.D(DATA_IN), .en(and_13_out), .clk(CLK), .Q(register_13_q), .clr(1'b0));
  and and_13 (and_13_out, LOAD, decoder_1_out12);
  Register #(.width(32)) register_14 (.D(DATA_IN), .en(and_14_out), .clk(CLK), .Q(register_14_q), .clr(1'b0));
  and and_14 (and_14_out, LOAD, decoder_1_out13);
  Register #(.width(32)) register_15 (.D(DATA_IN), .en(and_15_out), .clk(CLK), .Q(register_15_q), .clr(1'b0));
  and and_15 (and_15_out, LOAD, decoder_1_out14);
  Register #(.width(32)) register_16 (.D(DATA_IN), .en(and_16_out), .clk(CLK), .Q(register_16_q), .clr(1'b0));
  and and_16 (and_16_out, LOAD, decoder_1_out15);
  Register #(.width(32)) register_17 (.D(DATA_IN), .en(and_17_out), .clk(CLK), .Q(register_17_q), .clr(1'b0));
  and and_17 (and_17_out, LOAD, decoder_1_out16);
  Register #(.width(32)) register_18 (.D(DATA_IN), .en(and_18_out), .clk(CLK), .Q(register_18_q), .clr(1'b0));
  and and_18 (and_18_out, LOAD, decoder_1_out17);
  Register #(.width(32)) register_19 (.D(DATA_IN), .en(and_19_out), .clk(CLK), .Q(register_19_q), .clr(1'b0));
  and and_19 (and_19_out, LOAD, decoder_1_out18);
  Register #(.width(32)) register_20 (.D(DATA_IN), .en(and_20_out), .clk(CLK), .Q(register_20_q), .clr(1'b0));
  and and_20 (and_20_out, LOAD, decoder_1_out19);
  Register #(.width(32)) register_21 (.D(DATA_IN), .en(and_21_out), .clk(CLK), .Q(register_21_q), .clr(1'b0));
  and and_21 (and_21_out, LOAD, decoder_1_out20);
  Register #(.width(32)) register_22 (.D(DATA_IN), .en(and_22_out), .clk(CLK), .Q(register_22_q), .clr(1'b0));
  and and_22 (and_22_out, LOAD, decoder_1_out21);
  Register #(.width(32)) register_23 (.D(DATA_IN), .en(and_23_out), .clk(CLK), .Q(register_23_q), .clr(1'b0));
  and and_23 (and_23_out, LOAD, decoder_1_out22);
  Register #(.width(32)) register_24 (.D(DATA_IN), .en(and_24_out), .clk(CLK), .Q(register_24_q), .clr(1'b0));
  and and_24 (and_24_out, LOAD, decoder_1_out23);
  Register #(.width(32)) register_25 (.D(DATA_IN), .en(and_25_out), .clk(CLK), .Q(register_25_q), .clr(1'b0));
  and and_25 (and_25_out, LOAD, decoder_1_out24);
  Register #(.width(32)) register_26 (.D(DATA_IN), .en(and_26_out), .clk(CLK), .Q(register_26_q), .clr(1'b0));
  and and_26 (and_26_out, LOAD, decoder_1_out25);
  Register #(.width(32)) register_27 (.D(DATA_IN), .en(and_27_out), .clk(CLK), .Q(register_27_q), .clr(1'b0));
  and and_27 (and_27_out, LOAD, decoder_1_out26);
  Register #(.width(32)) register_28 (.D(DATA_IN), .en(and_28_out), .clk(CLK), .Q(register_28_q), .clr(1'b0));
  and and_28 (and_28_out, LOAD, decoder_1_out27);
  Register #(.width(32)) register_29 (.D(DATA_IN), .en(and_29_out), .clk(CLK), .Q(register_29_q), .clr(1'b0));
  and and_29 (and_29_out, LOAD, decoder_1_out28);
  Register #(.width(32)) register_30 (.D(DATA_IN), .en(and_30_out), .clk(CLK), .Q(register_30_q), .clr(1'b0));
  and and_30 (and_30_out, LOAD, decoder_1_out29);
  Register #(.width(32)) register_31 (.D(DATA_IN), .en(and_31_out), .clk(CLK), .Q(register_31_q), .clr(1'b0));
  and and_31 (and_31_out, LOAD, decoder_1_out30);
  Register #(.width(32)) register_32 (.D(DATA_IN), .en(and_32_out), .clk(CLK), .Q(register_32_q), .clr(1'b0));
  and and_32 (and_32_out, LOAD, decoder_1_out31);
  Multiplexer #(.select(5), .width(32), .enable("false")) multiplexer_1 (
    .in0(register_1_q), .in1(register_2_q), .in2(register_3_q), .in3(register_4_q), .in4(register_5_q),
    .in5(register_6_q), .in6(register_7_q), .in7(register_8_q), .in8(register_9_q), .in9(register_10_q),
    .in10(register_11_q), .in11(register_12_q), .in12(register_13_q), .in13(register_14_q),
    .in14(register_15_q), .in15(register_16_q), .in16(register_17_q), .in17(register_18_q),
    .in18(register_19_q), .in19(register_20_q), .in20(register_21_q), .in21(register_22_q),
    .in22(register_23_q), .in23(register_24_q), .in24(register_25_q), .in25(register_26_q),
    .in26(register_27_q), .in27(register_28_q), .in28(register_29_q), .in29(register_30_q),
    .in30(register_31_q), .in31(register_32_q), .out(DATA_A), .sel(ADDR_A));
  Multiplexer #(.select(5), .width(32), .enable("false")) multiplexer_2 (
    .in0(register_1_q), .in1(register_2_q), .in2(register_3_q), .in3(register_4_q), .in4(register_5_q),
    .in5(register_6_q), .in6(register_7_q), .in7(register_8_q), .in8(register_9_q), .in9(register_10_q),
    .in10(register_11_q), .in11(register_12_q), .in12(register_13_q), .in13(register_14_q),
    .in14(register_15_q), .in15(register_16_q), .in16(register_17_q), .in17(register_18_q),
    .in18(register_19_q), .in19(register_20_q), .in20(register_21_q), .in21(register_22_q),
    .in22(register_23_q), .in23(register_24_q), .in24(register_25_q), .in25(register_26_q),
    .in26(register_27_q), .in27(register_28_q), .in28(register_29_q), .in29(register_30_q),
    .in30(register_31_q), .in31(register_32_q), .out(DATA_B), .sel(ADDR_B));
endmodule

module D_MEM (
  input  [3:0] in_1,
  input  [31:0] in_2,
  input  in_3,
  input  [31:0] in_4,
  output [31:0] out_5
);

  wire undriven;
  wire [23:0] bit_extender_1_out;

  RAM #(.addrWidth(24), .dataWidth(32), .databus("bibus")) ram_1 (
    .addr(bit_extender_1_out), .we(undriven), .oe(1'b1), .clk(in_3), .din(in_4), .dout(out_5));
  Bit_Extender #(.in_width(32), .out_width(24), .\type ("zero")) bit_extender_1 (.in(in_2), .out(bit_extender_1_out));

  // Notes on the sheet:
  //   Data
  //   Address
endmodule

module I_MEM (
  input  [31:0] in_1,
  output [31:0] out_2
);

  wire [23:0] bit_extender_1_out;

  ROM #(.addrWidth(24), .dataWidth(32)) rom_1 (.addr(bit_extender_1_out), .data(out_2));
  Bit_Extender #(.in_width(32), .out_width(24), .\type ("zero")) bit_extender_1 (.in(in_1), .out(bit_extender_1_out));
endmodule

module ALU (
  input  [3:0] in_1,
  input  [31:0] ALUSrcA,
  input  [31:0] in_3,
  output [31:0] out_4
);

  wire ADD, AND, comparator_1_lt, comparator_2_lt, LUI, multiplexer_4_out, multiplexer_5_out, not_1_out,
       not_2_out, not_3_out, not_4_out, not_5_out, not_6_out, not_7_out, not_8_out, not_9_out, not_10_out,
       not_11_out, not_12_out, not_13_out, not_14_out, not_15_out, not_16_out, not_17_out, not_18_out,
       not_19_out, not_20_out, not_21_out, not_22_out, not_23_out, not_24_out, not_25_out, not_26_out, OR,
       SLL, SLT, SLTU, SRA, SRL, SUB, XOR;
  wire [4:0] bit_extender_1_out;
  wire [31:0] adder_1_out, and_12_out, bit_extender_2_out, bit_extender_3_out, multiplexer_1_out,
       multiplexer_2_out, multiplexer_3_out, multiplexer_6_out, multiplexer_7_out, multiplexer_8_out,
       multiplexer_9_out, multiplexer_10_out, or_1_out, or_2_out, shifter_1_out, shifter_2_out,
       shifter_3_out, subtractor_1_out, xor_1_out;

  not not_1 (not_1_out, in_1[3]);
  not not_2 (not_2_out, in_1[2]);
  not not_3 (not_3_out, in_1[1]);
  not not_4 (not_4_out, in_1[0]);
  not not_5 (not_5_out, in_1[2]);
  not not_6 (not_6_out, in_1[1]);
  not not_7 (not_7_out, in_1[0]);
  not not_8 (not_8_out, in_1[3]);
  not not_9 (not_9_out, in_1[2]);
  not not_10 (not_10_out, in_1[1]);
  not not_11 (not_11_out, in_1[3]);
  not not_12 (not_12_out, in_1[2]);
  not not_13 (not_13_out, in_1[0]);
  not not_14 (not_14_out, in_1[3]);
  not not_15 (not_15_out, in_1[2]);
  not not_16 (not_16_out, in_1[3]);
  not not_17 (not_17_out, in_1[1]);
  not not_18 (not_18_out, in_1[0]);
  not not_19 (not_19_out, in_1[3]);
  not not_20 (not_20_out, in_1[1]);
  not not_21 (not_21_out, in_1[1]);
  not not_22 (not_22_out, in_1[3]);
  not not_23 (not_23_out, in_1[0]);
  not not_24 (not_24_out, in_1[3]);
  not not_25 (not_25_out, in_1[2]);
  not not_26 (not_26_out, in_1[1]);
  and and_1 (ADD, not_1_out, not_2_out, not_3_out, not_4_out);
  and and_2 (SUB, in_1[3], not_5_out, not_6_out, not_7_out);
  and and_3 (SLL, not_8_out, not_9_out, not_10_out, in_1[0]);
  and and_4 (SLT, not_11_out, not_12_out, in_1[1], not_13_out);
  and and_5 (SLTU, not_14_out, not_15_out, in_1[1], in_1[0]);
  and and_6 (XOR, not_16_out, in_1[2], not_17_out, not_18_out);
  and and_7 (SRL, not_19_out, in_1[2], not_20_out, in_1[0]);
  and and_8 (SRA, in_1[3], in_1[2], not_21_out, in_1[0]);
  and and_9 (OR, not_22_out, in_1[2], in_1[1], not_23_out);
  and and_10 (AND, not_24_out, in_1[2], in_1[1], in_1[0]);
  and and_11 (LUI, in_1[3], not_25_out, not_26_out, in_1[0]);
  Bit_Extender #(.in_width(32), .out_width(5), .\type ("zero")) bit_extender_1 (.in(in_3), .out(bit_extender_1_out));
  Adder #(.width(32)) adder_1 (.a(ALUSrcA), .b(in_3), .out(adder_1_out), .cin(1'b0));  // open: cout
  Subtractor #(.width(32)) subtractor_1 (.a(ALUSrcA), .b(in_3), .out(subtractor_1_out), .bin(1'b0));  // open: bout
  Shifter #(.width(32)) shifter_1 (.in(ALUSrcA), .\dist (bit_extender_1_out), .out(shifter_1_out));
  Comparator #(.width(32)) comparator_1 (.a(ALUSrcA), .b(in_3), .lt(comparator_1_lt));  // open: gt, eq
  Comparator #(.width(32), .mode("unsigned")) comparator_2 (
    .a(ALUSrcA), .b(in_3), .lt(comparator_2_lt));  // open: gt, eq
  assign xor_1_out = ALUSrcA ^ in_3;  // XOR_Gate xor_1, 32 bits wide
  Shifter #(.width(32), .shift("lr")) shifter_2 (.in(ALUSrcA), .\dist (bit_extender_1_out), .out(shifter_2_out));
  Shifter #(.width(32), .shift("ar")) shifter_3 (.in(ALUSrcA), .\dist (bit_extender_1_out), .out(shifter_3_out));
  assign or_1_out = ALUSrcA | in_3;  // OR_Gate or_1, 32 bits wide
  assign and_12_out = ALUSrcA & in_3;  // AND_Gate and_12, 32 bits wide
  Multiplexer #(.width(32), .enable("false")) multiplexer_1 (
    .in0({32{1'b0}}), .in1(adder_1_out), .out(multiplexer_1_out), .sel(ADD));
  Multiplexer #(.width(32), .enable("false")) multiplexer_2 (
    .in0({32{1'b0}}), .in1(subtractor_1_out), .out(multiplexer_2_out), .sel(SUB));
  Multiplexer #(.width(32), .enable("false")) multiplexer_3 (
    .in0({32{1'b0}}), .in1(shifter_1_out), .out(multiplexer_3_out), .sel(SLL));
  Multiplexer #(.enable("false")) multiplexer_4 (.in0(1'b0), .in1(comparator_1_lt), .out(multiplexer_4_out), .sel(SLT));
  assign bit_extender_2_out = {{31{1'b0}}, multiplexer_4_out};  // Bit_Extender bit_extender_2
  assign bit_extender_3_out = {{31{1'b0}}, multiplexer_5_out};  // Bit_Extender bit_extender_3
  Multiplexer #(.enable("false")) multiplexer_5 (
    .in0(1'b0), .in1(comparator_2_lt), .out(multiplexer_5_out), .sel(SLTU));
  Multiplexer #(.width(32), .enable("false")) multiplexer_6 (
    .in0({32{1'b0}}), .in1(xor_1_out), .out(multiplexer_6_out), .sel(XOR));
  Multiplexer #(.width(32), .enable("false")) multiplexer_7 (
    .in0({32{1'b0}}), .in1(shifter_2_out), .out(multiplexer_7_out), .sel(SRL));
  Multiplexer #(.width(32), .enable("false")) multiplexer_8 (
    .in0({32{1'b0}}), .in1(shifter_3_out), .out(multiplexer_8_out), .sel(SRA));
  Multiplexer #(.width(32), .enable("false")) multiplexer_9 (
    .in0({32{1'b0}}), .in1(or_1_out), .out(multiplexer_9_out), .sel(OR));
  Multiplexer #(.width(32), .enable("false")) multiplexer_10 (
    .in0({32{1'b0}}), .in1(and_12_out), .out(multiplexer_10_out), .sel(AND));
  assign or_2_out = multiplexer_1_out | multiplexer_2_out | multiplexer_3_out | bit_extender_2_out | bit_extender_3_out | multiplexer_6_out | multiplexer_7_out | multiplexer_8_out | multiplexer_9_out | multiplexer_10_out;  // OR_Gate or_2, 32 bits wide
  Multiplexer #(.width(32), .enable("false")) multiplexer_11 (.in0(or_2_out), .in1(in_3), .out(out_4), .sel(LUI));

  // Notes on the sheet:
  //   ALUOp
  //   0000: Add
  //   1000: Sub
  //   0001: SLL
  //   0010: SLT
  //   0011: SLTU
  //   0100: XOR
  //   0101: SRL
  //   1101: SRA
  //   0110: OR
  //   0111: AND
  //   1001: LUI
  //   ALUSrcB
endmodule

module ImmGen (
  input  [4:0] in_1,
  input  [24:0] in_2,
  output [31:0] out_3
);

  wire [6:0] multiplexer_1_out;
  wire [31:0] bit_extender_1_out, bit_extender_2_out, bit_extender_3_out, bit_extender_4_out,
       multiplexer_2_out, multiplexer_3_out, multiplexer_4_out;

  Multiplexer #(.width(7), .enable("false")) multiplexer_1 (
    .in0(in_2[24:18]), .in1({7{1'b0}}), .out(multiplexer_1_out), .sel(in_1[4]));
  assign bit_extender_1_out = {{20{multiplexer_1_out[6]}}, {multiplexer_1_out, in_2[17:13]}};  // Bit_Extender bit_extender_1
  assign bit_extender_2_out = {{11{in_2[24]}}, {in_2[24], in_2[12:5], in_2[13], in_2[23:14], 1'b0}};  // Bit_Extender bit_extender_2
  assign bit_extender_3_out = {{19{in_2[24]}}, {in_2[24], in_2[0], in_2[23:18], in_2[4:1], 1'b0}};  // Bit_Extender bit_extender_3
  assign bit_extender_4_out = {{20{in_2[24]}}, {in_2[24:18], in_2[4:0]}};  // Bit_Extender bit_extender_4
  Multiplexer #(.width(32), .enable("false")) multiplexer_2 (
    .in0(bit_extender_1_out), .in1(bit_extender_2_out), .out(multiplexer_2_out), .sel(in_1[3]));
  Multiplexer #(.width(32), .enable("false")) multiplexer_3 (
    .in0(multiplexer_2_out), .in1({in_2[24:5], {12{1'b0}}}), .out(multiplexer_3_out), .sel(in_1[2]));
  Multiplexer #(.width(32), .enable("false")) multiplexer_4 (
    .in0(multiplexer_3_out), .in1(bit_extender_3_out), .out(multiplexer_4_out), .sel(in_1[1]));
  Multiplexer #(.width(32), .enable("false")) multiplexer_5 (
    .in0(multiplexer_4_out), .in1(bit_extender_4_out), .out(out_3), .sel(in_1[0]));

  // Notes on the sheet:
  //   ImmSrc
  //   000000: I_Type
  //   000001: S_Type
  //   000010: B_Type
  //   000100: U_Type
  //   001000: J_Type
  //   010000: shamt
  //   Instr[31:7]
  //   shamt
  //   J-Type
  //   U-Type
  //   B-Type
  //   S-Type
  //   I-Type
endmodule

module BranchCom (
  input  [31:0] in_1,
  input  [31:0] in_2,
  input  BrUn,
  output BrEq,
  output BrLT
);

  wire comparator_1_lt, comparator_2_lt;

  Comparator #(.width(32)) comparator_1 (.a(in_1), .b(in_2), .eq(BrEq), .lt(comparator_1_lt));  // open: gt
  Comparator #(.width(32), .mode("unsigned")) comparator_2 (.a(in_1), .b(in_2), .lt(comparator_2_lt));  // open: gt, eq
  Multiplexer #(.enable("false")) multiplexer_1 (.in0(comparator_1_lt), .in1(comparator_2_lt), .out(BrLT), .sel(BrUn));

  // Notes on the sheet:
  //   Signed
  //   Unsigned
endmodule
